// Logisim project DataMemory.circ as structural Verilog: 1 circuit, main circuit main
module main (
  input  Mem_Write,
  input  Mem_Read,
  input  [7:0] Address,
  input  [7:0] Write_Data,
  input  Clk,
  input  Cllr,
  output [7:0] out_7
);

  wire not_1_out;

  not not_1 (not_1_out, Clk);
  RAM #(.bus("separate")) ram_1 (
    .addr(Address), .din(Write_Data), .data(out_7), .str(Mem_Write), .clk(not_1_out), .ld(Mem_Read),
    .clr(Cllr));  // open: sel
endmodule
