// Logisim project Instruction memory.circ as structural Verilog: 1 circuit, main circuit Instruction Memory
module Instruction_Memory (
  input  [7:0] PC__write,
  input  Clock,
  input  Reset,
  output [7:0] PC_Read,
  output [3:0] Shft_Amnt,
  output [3:0] Dst_Reg,
  output [3:0] Src_Reg_2,
  output [3:0] Src_Reg_1,
  output [3:0] Opcode,
  output [7:0] Address_Immediate,
  output [7:0] Target_Jump_Address
);

  Register #(.trigger("falling")) PC (.D(PC__write), .Q(PC_Read), .clk(Clock), .clr(Reset));  // open: en
  ROM #(.dataWidth(20)) rom_1 (.addr(PC_Read), .data({Opcode, Src_Reg_1, Src_Reg_2, Address_Immediate}), .sel(1'b1));

  assign Dst_Reg = Address_Immediate[7:4];
  assign Shft_Amnt = Address_Immediate[3:0];
  assign Target_Jump_Address = {Src_Reg_1, Src_Reg_2};
endmodule
