// Logisim project Integrate.circ as structural Verilog: 1 circuit, main circuit main
module main (
  input  in_1
);

  wire alu_8_by_art_1_p5, clock_1_out, control_1_alusrc, control_1_beq, control_1_bneq, control_1_jump,
       control_1_memread, control_1_memtoreg, control_1_memwrite, control_1_regdst, control_1_regwrite,
       multiplexer_4_out, shift;
  wire [2:0] control_1_aluop;
  wire [3:0] instruction_memory_1_dst_reg, instruction_memory_1_opcode, instruction_memory_1_shft_amnt,
       instruction_memory_1_src_reg_1, instruction_memory_1_src_reg_2, multiplexer_1_out;
  wire [7:0] A, adder_1_out, adder_2_out, alu_8_by_art_1_p6, B, bit_extender_1_out, BshiftLogic,
       instruction_memory_1_address_immediate, instruction_memory_1_pc_read,
       instruction_memory_1_target_jump_address, main_1_out_7, multiplexer_2_out, multiplexer_5_out,
       multiplexer_7_out, multiplexer_8_out, registers_1_read_data_2;

  Clock clock_1 (.out(clock_1_out));
  Adder adder_1 (.a(instruction_memory_1_pc_read), .b(8'h1), .out(adder_1_out));  // open: cin, cout
  Instruction_Memory instruction_memory_1 (
    .PC__write(multiplexer_7_out), .Clock(clock_1_out), .Reset(in_1), .PC_Read(instruction_memory_1_pc_read),
    .Shft_Amnt(instruction_memory_1_shft_amnt), .Dst_Reg(instruction_memory_1_dst_reg),
    .Src_Reg_2(instruction_memory_1_src_reg_2), .Src_Reg_1(instruction_memory_1_src_reg_1),
    .Opcode(instruction_memory_1_opcode), .Address_Immediate(instruction_memory_1_address_immediate),
    .Target_Jump_Address(instruction_memory_1_target_jump_address));
  Adder adder_2 (.a(adder_1_out), .b(instruction_memory_1_address_immediate), .out(adder_2_out));  // open: cin, cout
  Control control_1 (
    .Opcode(instruction_memory_1_opcode), .AluOp(control_1_aluop), .AluSrc(control_1_alusrc),
    .bneq(control_1_bneq), .Beq(control_1_beq), .MemToReg(control_1_memtoreg), .MemWrite(control_1_memwrite),
    .MemRead(control_1_memread), .RegWrite(control_1_regwrite), .RegDst(control_1_regdst), .shift(shift),
    .jump(control_1_jump));
  Multiplexer #(.width(4), .enable("false")) multiplexer_1 (
    .in0(instruction_memory_1_src_reg_2), .in1(instruction_memory_1_dst_reg), .out(multiplexer_1_out),
    .sel(control_1_regdst));
  assign bit_extender_1_out = {{4{1'b0}}, instruction_memory_1_shft_amnt};  // Bit_Extender bit_extender_1
  Registers registers_1 (
    .Read_Register_1(instruction_memory_1_src_reg_1), .Write_register(multiplexer_1_out),
    .Read_Register_2(instruction_memory_1_src_reg_2), .Write_register_2(control_1_regwrite),
    .Clk(clock_1_out), .Clear(in_1), .Write_data(multiplexer_8_out), .Read_Data_1(A),
    .Read_Data_2(registers_1_read_data_2));
  Multiplexer #(.width(8), .enable("false")) multiplexer_2 (
    .in0(adder_1_out), .in1(adder_2_out), .out(multiplexer_2_out), .sel(multiplexer_4_out));
  Multiplexer #(.width(8), .enable("false")) multiplexer_3 (
    .in0(registers_1_read_data_2), .in1(instruction_memory_1_address_immediate), .out(B),
    .sel(control_1_alusrc));
  Multiplexer #(.enable("false")) multiplexer_4 (
    .in0(control_1_bneq), .in1(control_1_beq), .out(multiplexer_4_out), .sel(alu_8_by_art_1_p5));
  Multiplexer #(.width(8), .enable("false")) multiplexer_5 (
    .in0(A), .in1(bit_extender_1_out), .out(multiplexer_5_out), .sel(shift));
  // ALU_8_by_ART alu_8_by_art_1: pin names not known; wires that end beside it: multiplexer_5_out, BshiftLogic, control_1_beq, control_1_aluop, alu_8_by_art_1_p5, alu_8_by_art_1_p6
  Multiplexer #(.width(8), .enable("false")) multiplexer_6 (.in0(B), .in1(A), .out(BshiftLogic), .sel(shift));
  Multiplexer #(.width(8), .enable("false")) multiplexer_7 (
    .in0(multiplexer_2_out), .in1(instruction_memory_1_target_jump_address), .out(multiplexer_7_out),
    .sel(control_1_jump));
  DataMemory_main main_1 (
    .Address(alu_8_by_art_1_p6), .Write_Data(registers_1_read_data_2), .Clk(clock_1_out), .Cllr(in_1),
    .out_7(main_1_out_7), .Mem_Write(control_1_memwrite), .Mem_Read(control_1_memread));
  Multiplexer #(.width(8), .enable("false")) multiplexer_8 (
    .in0(alu_8_by_art_1_p6), .in1(main_1_out_7), .out(multiplexer_8_out), .sel(control_1_memtoreg));

  // Notes on the sheet:
  //   PC Read
  //   PC Write
  //   Clk
  //   Clr
  //   Shift amnt
  //   Dest Reg
  //   Src Reg 2
  //   Src Reg 1
  //   OpCode
  //   Address/immediate
  //   Target Jump Address
  //   ALUOP
  //   ALUSrc
  //   Bneq
  //   Beq
  //   MemToReg
  //   MemWrite
  //   MemRead
  //   RegWrite
  //   RegDest
  //   Shift
  //   Jump
  //   Read Register 1
  //   Read Register 2
  //   Write Data
  //   Write Register
  //   Read Data 1
  //   Read Data 2
  //   Clk
  //   Clr
  //   Mem Read
  //   Mem Write
  //   Address
  //   Write data
endmodule
