// Logisim project Registers.circ as structural Verilog: 1 circuit, main circuit Registers
module Registers (
  input  [3:0] Read_Register1,
  input  [3:0] Write_register,
  input  [3:0] Read_Register2,
  input  RegWrite,
  input  Clk,
  input  Clear,
  input  [7:0] WriteData,
  output [7:0] Read_Data_1,
  output [7:0] Read_Data_2
);

  wire and_1_out, and_2_out, and_3_out, and_4_out, and_5_out, and_6_out, decoder_1_out1, decoder_1_out2,
       decoder_1_out3, decoder_1_out4, decoder_1_out5, decoder_1_out6, multiplexer_1_out, multiplexer_3_out;
  wire [7:0] multiplexer_2_out, sp_q, t0_q, t1_q, t2_q, t3_q, t4_q, zero_q;

  Decoder #(.select(4), .enable("false")) decoder_1 (
    .out1(decoder_1_out1), .out2(decoder_1_out2), .out3(decoder_1_out3), .out4(decoder_1_out4),
    .out5(decoder_1_out5), .out6(decoder_1_out6), .sel(Write_register));  // open: out0, out7, out8, out9, out10, out11, out12, out13, out14, out15
  and and_1 (and_1_out, decoder_1_out1, RegWrite);
  and and_2 (and_2_out, decoder_1_out2, RegWrite);
  and and_3 (and_3_out, decoder_1_out3, RegWrite);
  and and_4 (and_4_out, decoder_1_out4, RegWrite);
  and and_5 (and_5_out, decoder_1_out5, RegWrite);
  and and_6 (and_6_out, decoder_1_out6, RegWrite);
  Multiplexer #(.enable("false")) multiplexer_1 (.in0(and_6_out), .in1(Clear), .out(multiplexer_1_out), .sel(Clear));
  Register zero (.D({8{1'b0}}), .Q(zero_q));  // open: en, clk, clr
  Register t0 (.D(WriteData), .en(and_1_out), .Q(t0_q), .clk(Clk), .clr(Clear));
  Register t1 (.D(WriteData), .en(and_2_out), .Q(t1_q), .clk(Clk), .clr(Clear));
  Register t2 (.D(WriteData), .en(and_3_out), .Q(t2_q), .clk(Clk), .clr(Clear));
  Register t3 (.D(WriteData), .en(and_4_out), .Q(t3_q), .clk(Clk), .clr(Clear));
  Register t4 (.D(WriteData), .en(and_5_out), .Q(t4_q), .clk(Clk), .clr(Clear));
  Multiplexer #(.width(8), .enable("false")) multiplexer_2 (
    .in0(WriteData), .in1({8{1'b1}}), .out(multiplexer_2_out), .sel(Clear));
  Register sp (.D(multiplexer_2_out), .en(multiplexer_1_out), .Q(sp_q), .clk(multiplexer_3_out));  // open: clr
  Multiplexer #(.enable("false")) multiplexer_3 (.in0(Clk), .in1(Clear), .out(multiplexer_3_out), .sel(Clear));
  Multiplexer #(.select(4), .width(8), .enable("false")) multiplexer_4 (
    .in0(zero_q), .in1(t0_q), .in2(t1_q), .in3(t2_q), .in4(t3_q), .in5(t4_q), .in6(sp_q), .out(Read_Data_1),
    .sel(Read_Register1));  // open: in7, in8, in9, in10, in11, in12, in13, in14, in15
  Multiplexer #(.select(4), .width(8), .enable("false")) multiplexer_5 (
    .in0(zero_q), .in1(t0_q), .in2(t1_q), .in3(t2_q), .in4(t3_q), .in5(t4_q), .in6(sp_q), .out(Read_Data_2),
    .sel(Read_Register2));  // open: in7, in8, in9, in10, in11, in12, in13, in14, in15
endmodule
