// Logisim project control.circ as structural Verilog: 1 circuit, main circuit Control
module Control (
  input  [3:0] Opcode,
  output [2:0] AluOp,
  output AluSrc,
  output bneq,
  output Beq,
  output MemToReg,
  output MemWrite,
  output MemRead,
  output RegWrite,
  output RegDst,
  output shift,
  output jump
);

  ROM #(.addrWidth(4), .dataWidth(13)) rom_1 (
    .addr(Opcode),
    .data({jump, shift, RegDst, RegWrite, MemRead, MemWrite, MemToReg, Beq, bneq, AluSrc, AluOp}));  // open: sel

  // Notes on the sheet:
  //   contents of rom_1 (hex, n*v repeats v):
  //   348 1000 88 e05 209 601 603 11 20a 602 600 604 208 e06 20b 21
endmodule
